# Fritzing sketch thermistor-hardware-connection (saved by Fritzing 0.9.3b)
breadboards: 1

parts:
  Thermistor = Temperature Sensor (Thermistor) [thermistor_type=NTC package=THT]
  Part1 = Arduino Uno (Rev3)
  R2 = Resistor [tolerance=±5% resistance=10k package=THT]

nets:
  GND: Thermistor.pin_0, Part1.GND
  N1: Thermistor.pin_1, Part1.A0, R2.Pin_1
  N2: Part1.5V, R2.Pin_0
