# Fritzing sketch thermistor-schematic-diagram (saved by Fritzing 0.9.3b)
breadboards: 1

parts:
  Thermistor = Temperature Sensor (Thermistor) [thermistor_type=NTC package=THT]
  Part1 = Arduino Uno (Rev3)
  R1 = Temperature Sensor (Thermistor) [thermistor_type=NTC package=THT]
  R2 = Resistor [tolerance=±5% resistance=220 package=THT]
  Resistor = Resistor [tolerance=±5% resistance=10k package=THT]

nets:
  GND: Thermistor.pin_0
  N1: Part1.A0, R1.pin_1, R2.Pin_1
  N2: Part1.5V, R2.Pin_0
  N3: Part1.GND, R1.pin_0
  5V: Resistor.Pin_0
  pin A0: Resistor.Pin_1
